// Logisim project vg-8s.circ as structural Verilog: 7 circuits, main circuit cpu
module cpu (
  output [7:0] EAB,
  output [7:0] EBUS8,
  output [7:0] out_3
);

  wire button_1_out, CE_PC, clock_1_out, CU6, CU7, CU12, CU13, CU14, CU15, CU22, CU23, d_ff_1_q, IOB_MBR,
       OE_ALU0, OE_ALU1, OE_IRH, OE_IRL, OE_MAR, OE_MBR, OE_OUT, OE_PC, OE_RAM, or_1_out, RE_SC, WE_A, WE_B,
       WE_C, WE_D, WE_IRH, WE_IRL, WE_MAR, WE_MBR, WE_OUT, WE_PSW, WE_RAM, WE_TMP;
  wire [3:0] counter_1_q;
  wire [7:0] A_data, A_out, alu_add_1_data0, alu_add_1_data1, B_data, B_out, C_data, C_out, D_2_data, D_data,
       D_out, IMM_data, IMM_out, IOB_out, MBR_data, OUTPUT_data, PC_q, PSW_data, PSW_out, reg8_1_data;
  wire [15:0] reg16_1_data;

  Clock clock_1 (.out(clock_1_out));
  Button button_1 (.out(button_1_out));
  LED led_1 (.in(WE_IRH));
  LED led_2 (.in(WE_IRL));
  LED led_3 (.in(OE_IRH));
  LED led_4 (.in(WE_A));
  LED led_5 (.in(WE_B));
  LED led_6 (.in(WE_C));
  LED led_7 (.in(WE_D));
  LED led_8 (.in(WE_TMP));
  LED led_9 (.in(WE_PSW));
  assign IOB_out = OE_PC ? PC_q : 8'bz;  // Controlled_Buffer IOB
  Counter PC (.D(IOB_out), .count(CE_PC), .Q(PC_q), .clk(clock_1_out), .clr(button_1_out));  // open: load, carry
  LED led_10 (.in(OE_PC));
  LED led_11 (.in(CE_PC));
  reg16 reg16_1 (
    .CLK(clock_1_out), .RST(button_1_out), .WEH(WE_IRH), .OEH(OE_IRH), .WEL(WE_IRL), .OEL(OE_IRL),
    .IN({EBUS8[7:3], EBUS8[3], EBUS8[1:0]}), .DATA(reg16_1_data), .OUT(IOB_out));
  LED led_12 (.in(OE_IRL));
  reg8 A (
    .CLK(clock_1_out), .RST(button_1_out), .WE(WE_A), .OE(1'b1), .IN({EBUS8[7:3], EBUS8[3], EBUS8[1:0]}),
    .DATA(A_data), .OUT(A_out));
  LED led_13 (.in(1'b1));
  reg8 B (
    .CLK(clock_1_out), .RST(button_1_out), .WE(WE_B), .OE(1'b1), .IN({EBUS8[7:3], EBUS8[3], EBUS8[1:0]}),
    .DATA(B_data), .OUT(B_out));
  LED led_14 (.in(1'b1));
  reg8 C (
    .CLK(clock_1_out), .RST(button_1_out), .WE(WE_C), .OE(1'b1), .IN({EBUS8[7:3], EBUS8[3], EBUS8[1:0]}),
    .DATA(C_data), .OUT(C_out));
  LED led_15 (.in(1'b1));
  reg8 D (
    .CLK(clock_1_out), .RST(button_1_out), .WE(WE_D), .OE(1'b1), .IN({EBUS8[7:3], EBUS8[3], EBUS8[1:0]}),
    .DATA(D_data), .OUT(D_out));
  LED led_16 (.in(1'b1));
  reg8 IMM (
    .CLK(clock_1_out), .RST(button_1_out), .WE(WE_TMP), .OE(1'b1), .IN({EBUS8[7:3], EBUS8[3], EBUS8[1:0]}),
    .DATA(IMM_data), .OUT(IMM_out));
  LED led_17 (.in(1'b1));
  reg8 PSW (
    .CLK(clock_1_out), .RST(button_1_out), .WE(WE_PSW), .OE(1'b1), .IN({EBUS8[7:3], EBUS8[3], EBUS8[1:0]}),
    .DATA(PSW_data), .OUT(PSW_out));
  LED led_18 (.in(1'b1));
  Hex_Digit_Display hex_digit_display_1 (.value(PC_q[3:0]));  // open: dp
  Hex_Digit_Display hex_digit_display_2 (.value(PC_q[7:4]));  // open: dp
  alu_add alu_add_1 (
    .A(A_out), .B(B_out), .C(C_out), .D(D_out), .TMP(IMM_out), .OPC(reg16_1_data[15:8]), .PSW(PSW_out),
    .OE0(OE_ALU0), .OE1(OE_ALU1), .DATA1(alu_add_1_data1), .DATA0(alu_add_1_data0),
    .OUT0({EBUS8[7:3], EBUS8[3], EBUS8[1:0]}), .OUT1({EBUS8[7:3], EBUS8[3], EBUS8[1:0]}));
  LED led_19 (.in(OE_ALU0));
  LED led_20 (.in(OE_ALU1));
  Hex_Digit_Display hex_digit_display_3 (.value(reg16_1_data[15:12]));  // open: dp
  Hex_Digit_Display hex_digit_display_4 (.value(reg16_1_data[11:8]));  // open: dp
  Hex_Digit_Display hex_digit_display_5 (.value(A_data[3:0]));  // open: dp
  Hex_Digit_Display hex_digit_display_6 (.value(A_data[7:4]));  // open: dp
  Hex_Digit_Display hex_digit_display_7 (.value(B_data[3:0]));  // open: dp
  Hex_Digit_Display hex_digit_display_8 (.value(B_data[7:4]));  // open: dp
  Hex_Digit_Display hex_digit_display_9 (.value(C_data[7:4]));  // open: dp
  Hex_Digit_Display hex_digit_display_10 (.value(C_data[3:0]));  // open: dp
  Hex_Digit_Display hex_digit_display_11 (.value(D_data[7:4]));  // open: dp
  Hex_Digit_Display hex_digit_display_12 (.value(D_data[3:0]));  // open: dp
  Hex_Digit_Display hex_digit_display_13 (.value(IMM_data[7:4]));  // open: dp
  Hex_Digit_Display hex_digit_display_14 (.value(IMM_data[3:0]));  // open: dp
  Hex_Digit_Display hex_digit_display_15 (.value(PSW_data[7:4]));  // open: dp
  Hex_Digit_Display hex_digit_display_16 (.value(PSW_data[3:0]));  // open: dp
  Hex_Digit_Display hex_digit_display_17 (.value(alu_add_1_data1[3:0]));  // open: dp
  Hex_Digit_Display hex_digit_display_18 (.value(alu_add_1_data1[7:4]));  // open: dp
  Hex_Digit_Display hex_digit_display_19 (.value(reg16_1_data[7:4]));  // open: dp
  Hex_Digit_Display hex_digit_display_20 (.value(reg16_1_data[3:0]));  // open: dp
  Hex_Digit_Display hex_digit_display_21 (.value(alu_add_1_data0[7:4]));  // open: dp
  Hex_Digit_Display hex_digit_display_22 (.value(alu_add_1_data0[3:0]));  // open: dp
  assign {EBUS8[7:3], EBUS8[3], EBUS8[1:0]} = IOB_MBR ? MBR_data : 8'bz;  // Controlled_Buffer IOB_2
  reg8 reg8_1 (
    .CLK(clock_1_out), .RST(button_1_out), .WE(WE_MAR), .OE(OE_MAR), .IN(IOB_out), .DATA(reg8_1_data),
    .OUT({EAB[0], EAB[1], EAB[2], EAB[3], EAB[4], EAB[5], EAB[6], EAB[7]}));
  LED led_21 (.in(OE_MAR));
  LED led_22 (.in(WE_MAR));
  reg8 MBR (
    .CLK(clock_1_out), .RST(button_1_out), .WE(WE_MBR), .OE(OE_MBR), .IN({EBUS8[7:3], EBUS8[3], EBUS8[1:0]}),
    .DATA(MBR_data), .OUT({EBUS8[7:3], EBUS8[3], EBUS8[1:0]}));
  LED led_23 (.in(OE_MBR));
  LED led_24 (.in(WE_MBR));
  reg8 OUTPUT (
    .CLK(clock_1_out), .RST(button_1_out), .WE(WE_OUT), .OE(OE_OUT), .IN({EBUS8[7:3], EBUS8[3], EBUS8[1:0]}),
    .DATA(OUTPUT_data), .OUT({EBUS8[7:3], EBUS8[3], EBUS8[1:0]}));
  LED led_25 (.in(WE_OUT));
  LED led_26 (.in(OE_OUT));
  D_Flip_Flop d_ff_1 (.clk(clock_1_out), .D(RE_SC), .Q(d_ff_1_q));  // open: Qn, preset, en, reset
  Hex_Digit_Display hex_digit_display_23 (.value(MBR_data[7:4]));  // open: dp
  reg8 D_2 (
    .CLK(clock_1_out), .RST(button_1_out), .WE(WE_IRH), .OE(1'b1), .IN({EBUS8[7:3], EBUS8[3], EBUS8[1:0]}),
    .DATA(D_2_data));  // open: OUT
  Counter #(.width(4), .max('hf)) counter_1 (
    .count(clock_1_out), .Q(counter_1_q), .clk(clock_1_out), .clr(or_1_out));  // open: load, D, carry
  or or_1 (or_1_out, button_1_out, d_ff_1_q);
  Hex_Digit_Display hex_digit_display_24 (.value(reg8_1_data[7:4]));  // open: dp
  Hex_Digit_Display hex_digit_display_25 (.value(reg8_1_data[3:0]));  // open: dp
  Hex_Digit_Display hex_digit_display_26 (.value(MBR_data[3:0]));  // open: dp
  Hex_Digit_Display hex_digit_display_27 (.value(OUTPUT_data[7:4]));  // open: dp
  Hex_Digit_Display hex_digit_display_28 (.value(OUTPUT_data[3:0]));  // open: dp
  Hex_Digit_Display hex_digit_display_29 (.value(D_2_data[7:4]));  // open: dp
  control_unit control_unit_1 (
    .OPCODE(D_2_data), .CYCLE(counter_1_q), .WE_A(WE_A), .WE_B(WE_B), .WE_C(WE_C), .WE_D(WE_D),
    .OE_ALU0(OE_ALU0), .OE_ALU1(OE_ALU1), .OE_OUT(OE_OUT), .WE_OUT(WE_OUT), .OE_IRH(OE_IRH), .OE_IRL(OE_IRL),
    .WE_IRH(WE_IRH), .WE_IRL(WE_IRL), .OE_PC(OE_PC), .CE_PC(CE_PC), .out_16(CU13), .WE_PSW(WE_PSW),
    .OE_MAR(OE_MAR), .WE_MAR(WE_MAR), .OE_MBR(OE_MBR), .WE_MBR(WE_MBR), .OE_RAM(OE_RAM), .WE_RAM(WE_RAM),
    .IOB_MBR(IOB_MBR), .RE_SC(RE_SC), .out_15(CU12), .WE_TMP(WE_TMP), .out_17(CU14), .out_18(CU15),
    .out_25(CU22), .out_26(CU23), .out_9(CU6), .out_10(CU7));
  Hex_Digit_Display hex_digit_display_30 (.value(D_2_data[3:0]));  // open: dp
  Hex_Digit_Display hex_digit_display_31 (.value(counter_1_q));  // open: dp
  LED led_27 (.in(WE_RAM));
  LED led_28 (.in(OE_RAM));
  RAM #(.bus("separate")) ram_1 (
    .addr({EAB[0], EAB[1], EAB[2], EAB[3], EAB[4], EAB[5], EAB[6], EAB[7]}),
    .din({EBUS8[7:3], EBUS8[3], EBUS8[1:0]}), .data({EBUS8[7:3], EBUS8[3], EBUS8[1:0]}), .str(WE_RAM),
    .clk(clock_1_out), .ld(OE_RAM));  // open: sel, clr

  assign EBUS8[2] = EBUS8[3];
  assign out_3 = {EBUS8[7:3], EBUS8[3], EBUS8[1:0]};

  // Notes on the sheet:
  //   Internal Address Bus (4-bit)
  //   Internal Data Bus (8-bit)
  //   External Data Bus (8-bit)
  //   External Address Bus (4-bit)
endmodule

module memcell (
  input  CLK,
  input  WE,
  input  IN,
  input  OE,
  input  RST,
  output DATA,
  output OUT
);

  wire and_1_out, and_2_out, not_1_out, or_1_out;

  and and_1 (and_1_out, DATA, not_1_out);
  not not_1 (not_1_out, WE);
  and and_2 (and_2_out, WE, IN);
  D_Flip_Flop d_ff_1 (.clk(CLK), .D(or_1_out), .Q(DATA), .reset(RST));  // open: Qn, preset, en
  or or_1 (or_1_out, and_1_out, and_2_out);
  assign OUT = OE ? DATA : 1'bz;  // Controlled_Buffer controlled_buffer_1
endmodule

// REG4
module reg4 (
  input  CLK,
  input  RST,
  input  WE,
  input  OE,
  input  [3:0] IN,
  output [3:0] DATA,
  output [3:0] OUT
);

  memcell _0 (.WE(WE), .IN(IN[0]), .OE(OE), .RST(RST), .DATA(DATA[0]), .OUT(OUT[0]), .CLK(CLK));
  memcell _1 (.WE(WE), .IN(IN[1]), .OE(OE), .RST(RST), .DATA(DATA[1]), .OUT(OUT[1]), .CLK(CLK));
  memcell _2 (.WE(WE), .IN(IN[2]), .OE(OE), .RST(RST), .DATA(DATA[2]), .OUT(OUT[2]), .CLK(CLK));
  memcell _3 (.WE(WE), .IN(IN[3]), .OE(OE), .RST(RST), .DATA(DATA[3]), .OUT(OUT[3]), .CLK(CLK));
endmodule

// REG8
module reg8 (
  input  CLK,
  input  RST,
  input  WE,
  input  OE,
  input  [7:0] IN,
  output [7:0] DATA,
  output [7:0] OUT
);

  memcell _0 (.WE(WE), .IN(IN[0]), .OE(OE), .RST(RST), .DATA(DATA[0]), .OUT(OUT[0]), .CLK(CLK));
  memcell _1 (.WE(WE), .IN(IN[1]), .OE(OE), .RST(RST), .DATA(DATA[1]), .OUT(OUT[1]), .CLK(CLK));
  memcell _2 (.WE(WE), .IN(IN[2]), .OE(OE), .RST(RST), .DATA(DATA[2]), .OUT(OUT[2]), .CLK(CLK));
  memcell _3 (.WE(WE), .IN(IN[3]), .OE(OE), .RST(RST), .DATA(DATA[3]), .OUT(OUT[3]), .CLK(CLK));
  memcell _4 (.WE(WE), .IN(IN[4]), .OE(OE), .RST(RST), .DATA(DATA[4]), .OUT(OUT[4]), .CLK(CLK));
  memcell _5 (.WE(WE), .IN(IN[5]), .OE(OE), .RST(RST), .DATA(DATA[5]), .OUT(OUT[5]), .CLK(CLK));
  memcell _6 (.WE(WE), .IN(IN[6]), .OE(OE), .RST(RST), .DATA(DATA[6]), .OUT(OUT[6]), .CLK(CLK));
  memcell _7 (.WE(WE), .IN(IN[7]), .OE(OE), .RST(RST), .DATA(DATA[7]), .OUT(OUT[7]), .CLK(CLK));
endmodule

// REG16
module reg16 (
  input  CLK,
  input  RST,
  input  WEH,
  input  OEH,
  input  WEL,
  input  OEL,
  input  [7:0] IN,
  output [15:0] DATA,
  output [7:0] OUT
);

  memcell _0 (.WE(WEL), .IN(IN[0]), .OE(OEL), .RST(RST), .DATA(DATA[0]), .OUT(OUT[0]), .CLK(CLK));
  memcell _1 (.WE(WEL), .IN(IN[1]), .OE(OEL), .RST(RST), .DATA(DATA[1]), .OUT(OUT[1]), .CLK(CLK));
  memcell _2 (.WE(WEL), .IN(IN[2]), .OE(OEL), .RST(RST), .DATA(DATA[2]), .OUT(OUT[2]), .CLK(CLK));
  memcell _3 (.WE(WEL), .IN(IN[3]), .OE(OEL), .RST(RST), .DATA(DATA[3]), .OUT(OUT[3]), .CLK(CLK));
  memcell _4 (.WE(WEL), .IN(IN[4]), .OE(OEL), .RST(RST), .DATA(DATA[4]), .OUT(OUT[4]), .CLK(CLK));
  memcell _5 (.WE(WEL), .IN(IN[5]), .OE(OEL), .RST(RST), .DATA(DATA[5]), .OUT(OUT[5]), .CLK(CLK));
  memcell _6 (.WE(WEL), .IN(IN[6]), .OE(OEL), .RST(RST), .DATA(DATA[6]), .OUT(OUT[6]), .CLK(CLK));
  memcell _7 (.WE(WEL), .IN(IN[7]), .OE(OEL), .RST(RST), .DATA(DATA[7]), .OUT(OUT[7]), .CLK(CLK));
  memcell _8 (.WE(WEH), .IN(IN[0]), .OE(OEH), .RST(RST), .DATA(DATA[8]), .OUT(OUT[0]), .CLK(CLK));
  memcell _9 (.WE(WEH), .IN(IN[1]), .OE(OEH), .RST(RST), .DATA(DATA[9]), .OUT(OUT[1]), .CLK(CLK));
  memcell _10 (.WE(WEH), .IN(IN[2]), .OE(OEH), .RST(RST), .DATA(DATA[10]), .OUT(OUT[2]), .CLK(CLK));
  memcell _11 (.WE(WEH), .IN(IN[3]), .OE(OEH), .RST(RST), .DATA(DATA[11]), .OUT(OUT[3]), .CLK(CLK));
  memcell _12 (.WE(WEH), .IN(IN[4]), .OE(OEH), .RST(RST), .DATA(DATA[12]), .OUT(OUT[4]), .CLK(CLK));
  memcell _13 (.WE(WEH), .IN(IN[5]), .OE(OEH), .RST(RST), .DATA(DATA[13]), .OUT(OUT[5]), .CLK(CLK));
  memcell _14 (.WE(WEH), .IN(IN[6]), .OE(OEH), .RST(RST), .DATA(DATA[14]), .OUT(OUT[6]), .CLK(CLK));
  memcell _15 (.WE(WEH), .IN(IN[7]), .OE(OEH), .RST(RST), .DATA(DATA[15]), .OUT(OUT[7]), .CLK(CLK));
endmodule

module alu_add (
  input  [7:0] A,
  input  [7:0] B,
  input  [7:0] C,
  input  [7:0] D,
  input  [7:0] TMP,
  input  [7:0] OPC,
  input  [7:0] PSW,
  input  OE0,
  input  OE1,
  output [7:0] DATA1,
  output [7:0] DATA0,
  output [7:0] OUT0,
  output [7:0] OUT1
);

  wire adder_1_cout, and_1_out, and_2_out, comparator_1_lt, comparator_2_gt, comparator_3_lt,
       comparator_4_gt, comparator_5_lt, comparator_6_gt, controlled_buffer_6_out, decoder_1_out0,
       decoder_1_out1, decoder_1_out2, decoder_1_out3, decoder_2_out0, decoder_2_out1, decoder_2_out2,
       decoder_2_out3, decoder_3_out0, decoder_3_out1, decoder_3_out2, decoder_3_out3, subtractor_2_bout;
  wire [3:0] subtractor_1_out;
  wire [7:0] adder_1_out, controlled_buffer_2_out, divider_1_out, divider_1_rem, multiplexer_1_out,
       multiplexer_2_out, multiplexer_3_out, multiplexer_4_out, multiplexer_5_out, multiplexer_6_out,
       multiplexer_7_out, multiplexer_8_out, multiplexer_9_out, multiplier_1_cout, multiplier_1_out,
       subtractor_2_out, undriven;

  Comparator comparator_1 (.a(OPC), .b(8'h20), .lt(comparator_1_lt));  // open: gt, eq
  Comparator comparator_2 (.a(OPC), .b(8'hf), .gt(comparator_2_gt));  // open: eq, lt
  Comparator comparator_3 (.a(OPC), .b(8'h5f), .lt(comparator_3_lt));  // open: gt, eq
  Comparator comparator_4 (.a(OPC), .b(8'h20), .gt(comparator_4_gt));  // open: eq, lt
  Comparator comparator_5 (.a(OPC), .b(8'h7f), .lt(comparator_5_lt));  // open: gt, eq
  Comparator comparator_6 (.a(OPC), .b(8'h60), .gt(comparator_6_gt));  // open: eq, lt
  and and_1 (and_1_out, comparator_1_lt, comparator_2_gt);
  Decoder #(.select(2), .enable("false")) decoder_1 (
    .out0(decoder_1_out0), .out1(decoder_1_out1), .out2(decoder_1_out2), .out3(decoder_1_out3), .sel(OPC[3:2]));
  and and_2 (and_2_out, comparator_3_lt, comparator_4_gt);
  Decoder #(.select(2), .enable("false")) decoder_2 (
    .out0(decoder_2_out0), .out1(decoder_2_out1), .out2(decoder_2_out2), .out3(decoder_2_out3), .sel(OPC[3:2]));
  Subtractor #(.width(4)) subtractor_1 (.a(OPC[7:4]), .b(4'b0010), .out(subtractor_1_out));  // open: bin, bout
  // AND_Gate and_3 has open pins: in0=comparator_5_lt, in1=comparator_6_gt, out=open
  Multiplexer #(.select(2), .width(8)) multiplexer_1 (
    .in0(TMP), .in1(B), .in2(C), .in3(D), .out(multiplexer_1_out), .sel(OPC[3:2]), .en(and_1_out));
  Multiplexer #(.select(2), .width(8)) multiplexer_2 (
    .in0(TMP), .in1(B), .in2(C), .in3(D), .out(multiplexer_2_out), .sel(OPC[3:2]), .en(and_2_out));
  assign {DATA0[0], DATA0[1], DATA0[2], DATA0[3], DATA0[4], DATA0[5], DATA0[6], DATA0[7]} = decoder_1_out0 ? multiplexer_1_out : 8'bz;  // Controlled_Buffer controlled_buffer_1
  assign controlled_buffer_2_out = decoder_2_out0 ? multiplexer_2_out : 8'bz;  // Controlled_Buffer controlled_buffer_2
  Decoder #(.select(2), .enable("false")) decoder_3 (
    .out0(decoder_3_out0), .out1(decoder_3_out1), .out2(decoder_3_out2), .out3(decoder_3_out3),
    .sel(subtractor_1_out[1:0]));
  Multiplexer #(.select(2), .width(8)) multiplexer_3 (
    .in0(TMP), .in1(A), .in2(C), .in3(D), .out(multiplexer_3_out), .sel(OPC[3:2]), .en(and_1_out));
  assign {DATA0[0], DATA0[1], DATA0[2], DATA0[3], DATA0[4], DATA0[5], DATA0[6], DATA0[7]} = decoder_1_out1 ? multiplexer_3_out : 8'bz;  // Controlled_Buffer controlled_buffer_3
  Multiplexer #(.select(2), .width(8)) multiplexer_4 (
    .in0(undriven), .in1(A), .in2(C), .in3(D), .out(multiplexer_4_out), .sel(OPC[3:2]), .en(and_2_out));
  assign controlled_buffer_2_out = decoder_2_out1 ? multiplexer_4_out : 8'bz;  // Controlled_Buffer controlled_buffer_4
  Adder adder_1 (
    .a(multiplexer_9_out), .b(controlled_buffer_2_out), .out(adder_1_out), .cout(adder_1_cout));  // open: cin
  assign {DATA0[0], DATA0[1], DATA0[2], DATA0[3], DATA0[4], DATA0[5], DATA0[6], DATA0[7]} = decoder_3_out0 ? adder_1_out : 8'bz;  // Controlled_Buffer controlled_buffer_5
  assign controlled_buffer_6_out = decoder_3_out0 ? adder_1_cout : 1'bz;  // Controlled_Buffer controlled_buffer_6
  assign controlled_buffer_6_out = decoder_3_out1 ? subtractor_2_bout : 1'bz;  // Controlled_Buffer controlled_buffer_7
  Multiplexer #(.select(2), .width(8)) multiplexer_5 (
    .in0(TMP), .in1(A), .in2(B), .in3(D), .out(multiplexer_5_out), .sel(OPC[3:2]), .en(and_1_out));
  assign {DATA0[0], DATA0[1], DATA0[2], DATA0[3], DATA0[4], DATA0[5], DATA0[6], DATA0[7]} = decoder_1_out2 ? multiplexer_5_out : 8'bz;  // Controlled_Buffer controlled_buffer_8
  Multiplexer #(.select(2), .width(8)) multiplexer_6 (
    .in0(TMP), .in1(A), .in2(B), .in3(D), .out(multiplexer_6_out), .sel(OPC[3:2]), .en(and_2_out));
  assign controlled_buffer_2_out = decoder_2_out2 ? multiplexer_6_out : 8'bz;  // Controlled_Buffer controlled_buffer_9
  Subtractor subtractor_2 (
    .a(multiplexer_9_out), .b(controlled_buffer_2_out), .out(subtractor_2_out), .bout(subtractor_2_bout));  // open: bin
  assign {DATA0[0], DATA0[1], DATA0[2], DATA0[3], DATA0[4], DATA0[5], DATA0[6], DATA0[7]} = decoder_3_out1 ? subtractor_2_out : 8'bz;  // Controlled_Buffer controlled_buffer_10
  assign {DATA1[0], DATA1[1], DATA1[2], DATA1[3], DATA1[4], DATA1[5], DATA1[6], DATA1[7]} = {{7{controlled_buffer_6_out}}, controlled_buffer_6_out};  // Bit_Extender bit_extender_1
  Multiplexer #(.select(2), .width(8)) multiplexer_7 (
    .in0(TMP), .in1(A), .in2(B), .in3(C), .out(multiplexer_7_out), .sel(OPC[3:2]), .en(and_1_out));
  Multiplexer #(.select(2), .width(8)) multiplexer_8 (
    .in0(TMP), .in1(A), .in2(B), .in3(C), .out(multiplexer_8_out), .sel(OPC[3:2]), .en(and_2_out));
  assign controlled_buffer_2_out = decoder_2_out3 ? multiplexer_8_out : 8'bz;  // Controlled_Buffer controlled_buffer_11
  Multiplier multiplier_1 (
    .a(multiplexer_9_out), .b(controlled_buffer_2_out), .out(multiplier_1_out), .cout(multiplier_1_cout));  // open: cin
  assign {DATA1[0], DATA1[1], DATA1[2], DATA1[3], DATA1[4], DATA1[5], DATA1[6], DATA1[7]} = decoder_3_out2 ? multiplier_1_cout : 8'bz;  // Controlled_Buffer controlled_buffer_12
  assign {DATA0[0], DATA0[1], DATA0[2], DATA0[3], DATA0[4], DATA0[5], DATA0[6], DATA0[7]} = decoder_3_out2 ? multiplier_1_out : 8'bz;  // Controlled_Buffer controlled_buffer_13
  assign {DATA0[0], DATA0[1], DATA0[2], DATA0[3], DATA0[4], DATA0[5], DATA0[6], DATA0[7]} = decoder_1_out3 ? multiplexer_7_out : 8'bz;  // Controlled_Buffer controlled_buffer_14
  Multiplexer #(.select(2), .width(8)) multiplexer_9 (
    .in0(A), .in1(B), .in2(C), .in3(D), .out(multiplexer_9_out), .sel(OPC[3:2]), .en(and_2_out));
  Divider divider_1 (
    .a(multiplexer_9_out), .b(controlled_buffer_2_out), .out(divider_1_out), .rem(divider_1_rem));  // open: upper
  assign {DATA0[0], DATA0[1], DATA0[2], DATA0[3], DATA0[4], DATA0[5], DATA0[6], DATA0[7]} = decoder_3_out3 ? divider_1_out : 8'bz;  // Controlled_Buffer controlled_buffer_15
  assign {DATA1[0], DATA1[1], DATA1[2], DATA1[3], DATA1[4], DATA1[5], DATA1[6], DATA1[7]} = decoder_3_out3 ? divider_1_rem : 8'bz;  // Controlled_Buffer controlled_buffer_16
  assign OUT0 = OE0 ? {DATA0[0], DATA0[1], DATA0[2], DATA0[3], DATA0[4], DATA0[5], DATA0[6], DATA0[7]} : 8'bz;  // Controlled_Buffer controlled_buffer_17
  assign OUT1 = OE1 ? {DATA1[0], DATA1[1], DATA1[2], DATA1[3], DATA1[4], DATA1[5], DATA1[6], DATA1[7]} : 8'bz;  // Controlled_Buffer controlled_buffer_18

  // Notes on the sheet:
  //   MOV
  //   ARTH
  //   LOGIC
endmodule

module control_unit (
  input  [7:0] OPCODE,
  input  [3:0] CYCLE,
  output WE_A,
  output WE_B,
  output WE_C,
  output WE_D,
  output WE_TMP,
  output WE_PSW,
  output out_9,
  output out_10,
  output OE_ALU0,
  output OE_ALU1,
  output OE_OUT,
  output WE_OUT,
  output out_15,
  output out_16,
  output out_17,
  output out_18,
  output OE_PC,
  output CE_PC,
  output OE_IRH,
  output WE_IRH,
  output OE_IRL,
  output WE_IRL,
  output out_25,
  output out_26,
  output OE_MAR,
  output WE_MAR,
  output OE_MBR,
  output WE_MBR,
  output OE_RAM,
  output WE_RAM,
  output IOB_MBR,
  output RE_SC
);

  ROM #(.addrWidth(12), .dataWidth(32)) rom_1 (
    .addr({OPCODE, CYCLE}),
    .data({RE_SC, IOB_MBR, WE_RAM, OE_RAM, WE_MBR, OE_MBR, WE_MAR, OE_MAR, out_26, out_25, WE_IRL, OE_IRL, WE_IRH, OE_IRH, CE_PC, OE_PC, out_18, out_17, out_16, out_15, WE_OUT, OE_OUT, OE_ALU1, OE_ALU0, out_10, out_9, WE_PSW, WE_TMP, WE_D, WE_C, WE_B, WE_A}));  // open: sel

  // Notes on the sheet:
  //   contents of rom_1 (hex, n*v repeats v):
  //   2010000 19000000 40a0000 2010000 19000000 84020001 10*0 2010000 19000000 40a0000 2010000 19000000
  //   84020002 10*0 2010000 19000000 40a0000 2010000 19000000 84020004 10*0 2010000 19000000 40a0000
  //   2010000 19000000 84020008 10*0 2010000 19000000 40a0000 13*0 2010000 19000000 40a0000 13*0 2010000
  //   19000000 40a0000 13*0 2010000 19000000 40a0000 13*0 2010000 19000000 40a0000 13*0 2010000 19000000
  //   40a0000 13*0 2010000 19000000 40a0000 13*0 2010000 19000000 40a0000 13*0 2010000 19000000 40a0000
  //   13*0 2010000 19000000 40a0000 13*0 2010000 19000000 40a0000 13*0 2010000 19000000 40a0000 13*0
  //   2010000 19000000 40a0000 900 80000401 11*0 2010000 19000000 40a0000 900 80000401 11*0 2010000
  //   19000000 40a0000 900 80000401 11*0 2010000 19000000 40a0000 900 80000401 11*0 2010000 19000000
  //   40a0000 13*0 2010000 19000000 40a0000 13*0 2010000 19000000 40a0000 13*0 2010000 19000000 40a0000
  //   13*0 2010000 19000000 40a0000 13*0 2010000 19000000 40a0000 13*0 2010000 19000000 40a0000 13*0
  //   2010000 19000000 40a0000 13*0 2010000 19000000 40a0000 13*0 2010000 19000000 40a0000 13*0 2010000
  //   19000000 40a0000 13*0 2010000 19000000 40a0000 13*0 2010000 19000000 40a0000 13*0 2010000 19000000
  //   40a0000 13*0 2010000 19000000 40a0000 13*0 2010000 19000000 40a0000 13*0 2010000 19000000 40a0000
  //   13*0 2010000 19000000 40a0000 13*0 2010000 19000000 40a0000 13*0 2010000 19000000 40a0000 13*0
  //   2010000 19000000 40a0000 13*0 2010000 19000000 40a0000 13*0 2010000 19000000 40a0000 13*0 2010000
  //   19000000 40a0000 13*0 2010000 19000000 40a0000 13*0 2010000 19000000 40a0000 13*0 2010000 19000000
  //   40a0000 13*0 2010000 19000000 40a0000 13*0 2010000 19000000 40a0000 13*0 2010000 19000000 40a0000
  //   13*0 2010000 19000000 40a0000 13*0 2010000 19000000 40a0000 13*0 2010000 19000000 40a0000 13*0
  //   2010000 19000000 40a0000 13*0 2010000 19000000 40a0000 13*0 2010000 19000000 40a0000 13*0 2010000
  //   19000000 40a0000 13*0 2010000 19000000 40a0000 13*0 2010000 19000000 40a0000 13*0 2010000 19000000
  //   40a0000 13*0 2010000 19000000 40a0000 13*0 2010000 19000000 40a0000 13*0 2010000 19000000 40a0000
  //   13*0 2010000 19000000 40a0000 13*0 2010000 19000000 40a0000 13*0 2010000 19000000 40a0000 13*0
  //   2010000 19000000 40a0000 13*0 2010000 19000000 40a0000 13*0 2010000 19000000 40a0000 13*0 2010000
  //   19000000 40a0000 13*0 2010000 19000000 40a0000 13*0 2010000 19000000 40a0000 13*0 2010000 19000000
  //   40a0000 13*0 2010000 19000000 40a0000 13*0 2010000 19000000 40a0000 13*0 2010000 19000000 40a0000
  //   13*0 2010000 19000000 40a0000 13*0 2010000 19000000 40a0000 13*0 2010000 19000000 40a0000 13*0
  //   2010000 19000000 40a0000 13*0 2010000 19000000 40a0000 13*0 2010000 19000000 40a0000 13*0 2010000
  //   19000000 40a0000 13*0 2010000 19000000 40a0000 13*0 2010000 19000000 40a0000 13*0 2010000 19000000
  //   40a0000 13*0 2010000 19000000 40a0000 13*0 2010000 19000000 40a0000 13*0 2010000 19000000 40a0000
  //   13*0 2010000 19000000 40a0000 13*0 2010000 19000000 40a0000 13*0 2010000 19000000 40a0000 13*0
  //   2010000 19000000 40a0000 13*0 2010000 19000000 40a0000 13*0 2010000 19000000 40a0000 13*0 2010000
  //   19000000 40a0000 13*0 2010000 19000000 40a0000 13*0 2010000 19000000 40a0000 13*0 2010000 19000000
  //   40a0000 13*0 2010000 19000000 40a0000
endmodule
